# Fritzing sketch nalle (saved by Fritzing 0.8.5b)
breadboards: 1

parts:
  Part1 = Arduino Uno (Rev3)
  J1 = Piezo Speaker
  R1 = Photocell (LDR) [package=THT]
  J2 = Basic Servo
  J3 = Basic Servo
  R6 = Resistor [tolerance=±10% resistance=10k package=THT]
  R7 = Resistor [tolerance=±5% resistance=10k package=THT]
  S1 = Tilt Switch [package=THT]

nets (from the schematic view):
  N1: Part1.A0, R1.pin_1, R6.Pin_0
  N2: Part1.D10_PWM/SS, R7.Pin_0, S1.Pin_1
  N3: Part1.D12/MISO, J1.pin2
  GND: Part1.GND, J1.pin1, J2.gnd, J3.gnd, R6.Pin_1, R7.Pin_1
  N4: Part1.D4, J2.pulse
  N5: Part1.D6_PWM, J3.pulse
  VCC: Part1.5V, R1.pin_0, J2.vcc, J3.vcc, S1.Pin_2
